# Fritzing sketch circuit (saved by Fritzing 0.9.3b)
breadboards: 1

parts:
  Componente1 = Arduino Uno (Rev3)
  LCD1 = LCD screen
  S1 = Pushbutton [package="[THT]"]
  S2 = Pushbutton [package="[THT]"]
  S3 = Pushbutton [package="[THT]"]
  S4 = Pushbutton [package="[THT]"]
  S5 = Pushbutton [package="[THT]"]
  S6 = Pushbutton [package="[THT]"]
  S7 = Pushbutton [package="[THT]"]
  R1 = Resistor [tolerance=±5% resistance=220 package=THT]
  R2 = Trimmer Potentiometer [maximum_resistance=10kΩ package=THT]
  LED1 = LED - 5mm [color="Blue (470nm)" package="5 mm [THT]"]
  R3 = Resistor [tolerance=±5% resistance=1.5k package=THT]

nets:
  N1: Componente1.A0, S7.Pin_3, S7.Pin_4
  N2: Componente1.A1, S2.Pin_3, S2.Pin_4
  N3: Componente1.A2, S6.Pin_3, S6.Pin_4
  N4: Componente1.D8, R3.Pin_0
  N5: Componente1.D9_PWM, S3.Pin_3, S3.Pin_4
  N6: Componente1.D10_PWM/SS, S4.Pin_3, S4.Pin_4
  N7: Componente1.D11_PWM/MOSI, S5.Pin_3, S5.Pin_4
  N8: Componente1.D12/MISO, S1.Pin_3, S1.Pin_4
  GND: Componente1.GND, LCD1.VSS, LCD1.R/W, LCD1.LED-, S1.Pin_1, S1.Pin_2, S2.Pin_1, S2.Pin_2, S3.Pin_1, S3.Pin_2, S4.Pin_1, S4.Pin_2, S5.Pin_1, S5.Pin_2, S6.Pin_1, S6.Pin_2, S7.Pin_1, S7.Pin_2, R2.leg1, LED1.anode
  N9: Componente1.D2, LCD1.DB7
  N10: Componente1.D3_PWM, LCD1.DB6
  N11: Componente1.D4, LCD1.DB5
  N12: Componente1.D5_PWM, LCD1.DB4
  N13: Componente1.D6_PWM, LCD1.E
  N14: Componente1.D7, LCD1.RS
  5V: Componente1.5V, LCD1.VDD, R1.Pin_0, R2.leg2
  N15: LCD1.V0, R2.wiper
  N16: LCD1.LED+, R1.Pin_1
  N17: LED1.cathode, R3.Pin_1
